# Fritzing sketch circuit_01 (saved by Fritzing 0.7.7b)
breadboards: 1

parts:
  Arduino1 = Arduino
  LED1 = LED - 5mm [color="Red (633nm)" package="5 mm [THT]"]
  R1 = Resistor [tolerance=±5% resistance=220 package=THT]
  S1 = Pushbutton [package="[THT]"]
  R2 = Resistor [tolerance=±5% resistance=10k package=THT]
  R3 = Resistor [tolerance=±5% resistance=220 package=THT]
  LED2 = LED - 5mm [color="Red (633nm)" package="5 mm [THT]"]
  S2 = Pushbutton [package="[THT]"]
  R4 = Resistor [tolerance=±5% resistance=10k package=THT]
  R5 = Resistor [tolerance=±5% resistance=220 package=THT]
  R6 = Resistor [tolerance=±5% resistance=10k package=THT]
  S3 = Pushbutton [package="[THT]"]
  LED3 = LED - 5mm [color="Red (633nm)" package="5 mm [THT]"]
  R7 = Resistor [tolerance=±5% resistance=220 package=THT]
  R8 = Resistor [tolerance=±5% resistance=10k package=THT]
  S4 = Pushbutton [package="[THT]"]
  LED4 = LED - 5mm [color="Red (633nm)" package="5 mm [THT]"]
  J1 = Piezo Speaker
  R9 = Photocell (LDR) [package=THT]
  R10 = Resistor [tolerance=±5% resistance=10k package=THT]

nets:
  N1: Arduino1.GND, R1.Pin_0, R2.Pin_1, R3.Pin_0, R4.Pin_1, R5.Pin_0, R6.Pin_1, R7.Pin_0, R8.Pin_1, J1.pin1, R10.Pin_1
  N2: Arduino1.D12, J1.pin2
  N3: Arduino1.D11, LED1.anode
  N4: Arduino1.D9, LED2.anode
  N5: Arduino1.D8, S1.Pin_1, S1.Pin_2, R2.Pin_0
  N6: Arduino1.D7, S2.Pin_1, S2.Pin_2, R4.Pin_0
  N7: Arduino1.D6, LED3.anode
  N8: Arduino1.D4, R6.Pin_0, S3.Pin_1, S3.Pin_2
  N9: Arduino1.D3, LED4.anode
  N10: Arduino1.D2, R8.Pin_0, S4.Pin_1, S4.Pin_2
  N11: Arduino1.+5V, S2.Pin_3, S2.Pin_4, S3.Pin_3, S3.Pin_4, S4.Pin_3, S4.Pin_4, R9.pin_0
  N12: Arduino1.A0, R9.pin_1, R10.Pin_0
  N13: LED1.cathode, R1.Pin_1
  N14: S1.Pin_3, S1.Pin_4
  N15: R3.Pin_1, LED2.cathode
  N16: R5.Pin_1, LED3.cathode
  N17: R7.Pin_1, LED4.cathode
